// Digital circuit ACUMULADOR.dig as structural Verilog
module ACUMULADOR (
  input  CLR,
  input  CLK
);

  wire undriven, undriven_2, undriven_3;
  wire [7:0] d_ff_as_1_q, driver_1_out, driverinvsel_1_out;

  assign driver_1_out[0] = undriven ? d_ff_as_1_q[0] : 1'bz;  // Driver driver_1
  assign driverinvsel_1_out[0] = ~undriven_3 ? undriven_2 : 1'bz;  // DriverInvSel driverinvsel_1
  D_FF_AS d_ff_as_1 (.Set(1'b0), .D(driverinvsel_1_out[0]), .C(CLK), .Clr(CLR), .Q(d_ff_as_1_q[0]));  // open: nQ
  D_FF_AS d_ff_as_2 (.D(driverinvsel_1_out[1]), .C(CLK), .Clr(CLR), .Q(d_ff_as_1_q[1]));  // open: Set, nQ
  D_FF_AS d_ff_as_3 (.Set(1'b0), .D(driverinvsel_1_out[2]), .C(CLK), .Clr(CLR), .Q(d_ff_as_1_q[2]));  // open: nQ
  D_FF_AS d_ff_as_4 (.D(driverinvsel_1_out[3]), .C(CLK), .Clr(CLR), .Q(d_ff_as_1_q[3]));  // open: Set, nQ
  D_FF_AS d_ff_as_5 (.Set(1'b0), .D(driverinvsel_1_out[4]), .C(CLK), .Clr(CLR), .Q(d_ff_as_1_q[4]));  // open: nQ
  D_FF_AS d_ff_as_6 (.D(driverinvsel_1_out[5]), .C(CLK), .Clr(CLR), .Q(d_ff_as_1_q[5]));  // open: Set, nQ
  D_FF_AS d_ff_as_7 (.Set(1'b0), .D(driverinvsel_1_out[6]), .C(CLK), .Clr(CLR), .Q(d_ff_as_1_q[6]));  // open: nQ
  D_FF_AS d_ff_as_8 (.D(driverinvsel_1_out[7]), .C(CLK), .Clr(CLR), .Q(d_ff_as_1_q[7]));  // open: Set, nQ
  // Pins of 1 and 8 bits meet at driverinvsel_1_out
  // Pins of 1 and 8 bits meet at driver_1_out
  // Pins of 1 and 8 bits meet at d_ff_as_1_q

  // Notes on the sheet:
  //   ACUMULADOR
endmodule
