// Digital circuit CONTADOR DO PROGRAMA.dig as structural Verilog
module CONTADOR_DO_PROGRAMA (
  input  CLR,
  input  Cp,
  input  Ep,
  input  clk
);

  wire and_1_out, and_2_out, and_3_out;
  wire [3:0] driver_1_out, jk_ff_as_2_q;

  and and_1 (and_1_out, Cp, jk_ff_as_2_q[0]);
  JK_FF_AS jk_ff_as_1 (.Set(1'b0), .J(Cp), .C(clk), .K(Cp), .Clr(CLR), .Q(jk_ff_as_2_q[0]));  // open: nQ
  and and_2 (and_2_out, Cp, and_1_out, jk_ff_as_2_q[1]);
  JK_FF_AS jk_ff_as_2 (.Set(1'b0), .J(and_1_out), .C(clk), .K(and_1_out), .Clr(CLR), .Q(jk_ff_as_2_q[1]));  // open: nQ
  and and_3 (and_3_out, Cp, and_2_out, jk_ff_as_2_q[2]);
  JK_FF_AS jk_ff_as_3 (.Set(1'b0), .J(and_2_out), .C(clk), .K(and_2_out), .Clr(CLR), .Q(jk_ff_as_2_q[2]));  // open: nQ
  JK_FF_AS jk_ff_as_4 (.Set(1'b0), .J(and_3_out), .C(clk), .K(and_3_out), .Clr(CLR), .Q(jk_ff_as_2_q[3]));  // open: nQ
  Seven_Seg_Hex seven_seg_hex_1 (.d(driver_1_out), .dp(clk));
  assign driver_1_out = Ep ? jk_ff_as_2_q : 4'bz;  // Driver driver_1

  // Notes on the sheet:
  //   CONTADOR
endmodule
