// Digital circuit CONTADOR EM ANEL.dig as structural Verilog
module CONTADOR_EM_ANEL (
  input  CLK,
  output T1,
  output T2,
  output T3,
  output T4,
  output T5,
  output T6
);

  wire nor_1_out;

  D_FF d_ff_1 (.D(nor_1_out), .C(CLK), .Q(T1));  // open: nQ
  D_FF d_ff_2 (.D(T1), .C(CLK), .Q(T2));  // open: nQ
  nor nor_1 (nor_1_out, T6, T5, T4, T3, T2, T1);
  D_FF d_ff_3 (.D(T2), .C(CLK), .Q(T3));  // open: nQ
  D_FF d_ff_4 (.D(T3), .C(CLK), .Q(T4));  // open: nQ
  D_FF d_ff_5 (.D(T4), .C(CLK), .Q(T5));  // open: nQ
  D_FF d_ff_6 (.D(T5), .C(CLK), .Q(T6));  // open: nQ
endmodule
