// Digital circuit CONTROLADOR E SEQUENCIALIZADOR.dig as structural Verilog
module CONTROLADOR_E_SEQUENCIALIZADOR (
  input  _7,
  input  _6,
  input  _5,
  input  _4,
  input  CLK,
  output Cp,
  output Ep,
  output nLm,
  output nCE,
  output nLi,
  output nEi,
  output nLa,
  output Ea,
  output Su,
  output Eu,
  output nLb,
  output nLo,
  output HALT
);

  wire and_1_out, and_2_out, and_3_out, and_4_out, and_6_out, and_7_out, and_8_out, and_9_out, and_10_out,
       and_11_out, and_12_out, and_13_out, and_14_out, and_15_out, and_16_out, and_17_out, and_20_out,
       and_21_out, and_22_out, and_23_out, d_ff_3_q, d_ff_4_q, d_ff_5_q, d_ff_6_q, nor_1_out, not_1_out,
       not_2_out, not_3_out, not_4_out;

  not not_1 (not_1_out, _7);
  not not_2 (not_2_out, _6);
  not not_3 (not_3_out, _5);
  not not_4 (not_4_out, _4);
  and and_1 (and_1_out, _7, not_2_out, _5, _4);
  and and_2 (and_2_out, not_1_out, _6, not_3_out, _4);
  and and_3 (and_3_out, not_1_out, _6, _5, _4);
  and and_4 (and_4_out, not_1_out, not_2_out, not_3_out, not_4_out);
  and and_5 (HALT, not_1_out, _6, not_3_out, not_4_out);
  D_FF d_ff_1 (.D(nor_1_out), .C(CLK), .Q(Ep));  // open: nQ
  nor nor_1 (nor_1_out, d_ff_6_q, d_ff_5_q, d_ff_4_q, d_ff_3_q, Cp, Ep);
  D_FF d_ff_2 (.D(Ep), .C(CLK), .Q(Cp));  // open: nQ
  D_FF d_ff_3 (.D(Cp), .C(CLK), .Q(d_ff_3_q));  // open: nQ
  D_FF d_ff_4 (.D(d_ff_3_q), .C(CLK), .Q(d_ff_4_q));  // open: nQ
  D_FF d_ff_5 (.D(d_ff_4_q), .C(CLK), .Q(d_ff_5_q));  // open: nQ
  D_FF d_ff_6 (.D(d_ff_5_q), .C(CLK), .Q(d_ff_6_q));  // open: nQ
  and and_6 (and_6_out, and_1_out, d_ff_4_q);
  and and_7 (and_7_out, and_2_out, d_ff_4_q);
  and and_8 (and_8_out, and_3_out, d_ff_4_q);
  nor nor_2 (nLm, Ep, and_8_out, and_7_out, and_6_out);
  and and_9 (and_9_out, and_1_out, d_ff_5_q);
  and and_10 (and_10_out, and_2_out, d_ff_5_q);
  nor nor_3 (nCE, d_ff_3_q, and_11_out, and_10_out, and_9_out);
  and and_11 (and_11_out, and_3_out, d_ff_5_q);
  not not_5 (nLi, d_ff_3_q);
  and and_12 (and_12_out, and_1_out, d_ff_4_q);
  and and_13 (and_13_out, and_2_out, d_ff_4_q);
  nor nor_4 (nEi, and_14_out, and_13_out, and_12_out);
  and and_14 (and_14_out, and_3_out, d_ff_4_q);
  and and_15 (and_15_out, and_1_out, d_ff_5_q);
  and and_16 (and_16_out, and_2_out, d_ff_6_q);
  nor nor_5 (nLa, and_17_out, and_16_out, and_15_out);
  and and_17 (and_17_out, and_3_out, d_ff_6_q);
  and and_18 (Ea, and_4_out, d_ff_4_q);
  and and_19 (Su, and_3_out, d_ff_6_q);
  and and_20 (and_20_out, and_2_out, d_ff_6_q);
  or or_1 (Eu, and_21_out, and_20_out);
  and and_21 (and_21_out, and_3_out, d_ff_6_q);
  and and_22 (and_22_out, and_2_out, d_ff_5_q);
  and and_23 (and_23_out, and_3_out, d_ff_5_q);
  nor nor_6 (nLb, and_23_out, and_22_out);
  nand nand_1 (nLo, d_ff_4_q, and_4_out);

  // Notes on the sheet:
  //   CONTROLADOR / SEQUENCIALIZADOR
  //   DECODIFICADOR
  //   CONTADOR EM ANEL
  //   LDA
  //   ADD
  //   SUB
  //   OUT
  //   HLT
  //   T1
  //   T2
  //   T3
  //   T4
  //   T5
  //   T6
endmodule
