// Digital circuit DECODIFICADOR.dig as structural Verilog
module DECODIFICADOR (
  input  _7,
  input  _6,
  input  _5,
  input  _4,
  output LDA,
  output ADD,
  output SUB,
  output OUT,
  output HLT
);

  wire not_1_out, not_2_out, not_3_out, not_4_out;

  not not_1 (not_1_out, _7);
  not not_2 (not_2_out, _6);
  not not_3 (not_3_out, _5);
  not not_4 (not_4_out, _4);
  and and_1 (LDA, _7, not_2_out, _5, _4);
  and and_2 (ADD, not_1_out, _6, not_3_out, _4);
  and and_3 (SUB, not_1_out, _6, _5, _4);
  and and_4 (OUT, not_1_out, not_2_out, not_3_out, not_4_out);
  and and_5 (HLT, not_1_out, _6, not_3_out, not_4_out);

  // Notes on the sheet:
  //   DECODIFICADOR
endmodule
