// Digital circuit ENTRADA E REM.dig as structural Verilog
module ENTRADA_E_REM (
  input  CLK,
  input  CLR,
  input  LM
);

  wire not_1_out, undriven;
  wire [3:0] d_ff_as_1_q, driver_1_out;

  D_FF_AS d_ff_as_1 (.D(driver_1_out[3]), .C(CLK), .Clr(CLR), .Q(d_ff_as_1_q[3]));  // open: Set, nQ
  D_FF_AS d_ff_as_2 (.D(driver_1_out[2]), .C(CLK), .Clr(CLR), .Q(d_ff_as_1_q[2]));  // open: Set, nQ
  D_FF_AS d_ff_as_3 (.D(driver_1_out[1]), .C(CLK), .Clr(CLR), .Q(d_ff_as_1_q[1]));  // open: Set, nQ
  D_FF_AS d_ff_as_4 (.D(driver_1_out[0]), .C(CLK), .Clr(CLR), .Q(d_ff_as_1_q[0]));  // open: Set, nQ
  assign driver_1_out[0] = not_1_out ? undriven : 1'bz;  // Driver driver_1
  not not_1 (not_1_out, LM);
  // Pins of 1 and 4 bits meet at driver_1_out

  // Notes on the sheet:
  //   REM
endmodule
