// Digital circuit REGISTRADOR DE INTRUÇÕES.dig as structural Verilog
module \REGISTRADOR_DE_INTRUÇÕES  (
  input  CLR,
  input  CLK,
  input  Li,
  input  Ei
);

  wire not_1_out, not_2_out;
  wire [3:0] d_ff_as_1_nq, d_ff_as_5_nq, driver_1_out, driver_2_out, driver_3_out, undriven, undriven_2;

  D_FF_AS d_ff_as_1 (.Set(1'b0), .D(driver_1_out[3]), .C(CLK), .Clr(CLR), .nQ(d_ff_as_1_nq[3]));  // open: Q
  D_FF_AS d_ff_as_2 (.Set(1'b0), .D(driver_1_out[2]), .C(CLK), .Clr(CLR), .nQ(d_ff_as_1_nq[2]));  // open: Q
  D_FF_AS d_ff_as_3 (.Set(1'b0), .D(driver_1_out[1]), .C(CLK), .Clr(CLR), .nQ(d_ff_as_1_nq[1]));  // open: Q
  D_FF_AS d_ff_as_4 (.Set(1'b0), .D(driver_1_out[0]), .C(CLK), .Clr(CLR), .nQ(d_ff_as_1_nq[0]));  // open: Q
  D_FF_AS d_ff_as_5 (.Set(1'b0), .D(driver_3_out[3]), .C(CLK), .Clr(CLR), .nQ(d_ff_as_5_nq[3]));  // open: Q
  D_FF_AS d_ff_as_6 (.Set(1'b0), .D(driver_3_out[2]), .C(CLK), .Clr(CLR), .nQ(d_ff_as_5_nq[2]));  // open: Q
  D_FF_AS d_ff_as_7 (.Set(1'b0), .D(driver_3_out[1]), .C(CLK), .Clr(CLR), .nQ(d_ff_as_5_nq[1]));  // open: Q
  D_FF_AS d_ff_as_8 (.Set(1'b0), .D(driver_3_out[0]), .C(CLK), .Clr(CLR), .nQ(d_ff_as_5_nq[0]));  // open: Q
  assign driver_1_out = not_2_out ? undriven : 4'bz;  // Driver driver_1
  assign driver_2_out = not_1_out ? d_ff_as_5_nq : 4'bz;  // Driver driver_2
  not not_1 (not_1_out, Ei);
  not not_2 (not_2_out, Li);
  assign driver_3_out = not_2_out ? undriven_2 : 4'bz;  // Driver driver_3
endmodule
