// Digital circuit SAP-1.dig as structural Verilog
module SAP_1 (
  input  CLR,
  input  Cp,
  input  Ep,
  input  CLR_2,
  input  LM,
  input  [3:0] ENDE,
  input  RUN,
  input  [7:0] DADO,
  input  CE,
  input  in_10
);

  wire and_1_out, and_2_out, and_3_out, and_4_out, ESCREVER_out, not_1_out, not_2_out;
  wire [3:0] d_ff_as_1_q, driver_2_out, jk_ff_as_1_q, multiplexer_1_out;
  wire [7:0] ramdualport_1_d;

  D_FF_AS d_ff_as_1 (.Set(1'b0), .D(driver_2_out[3]), .C(in_10), .Clr(CLR_2), .Q(d_ff_as_1_q[3]));  // open: nQ
  and and_1 (and_1_out, Cp, jk_ff_as_1_q[0]);
  JK_FF_AS jk_ff_as_1 (.Set(1'b0), .J(Cp), .C(in_10), .K(Cp), .Clr(CLR), .Q(jk_ff_as_1_q[0]));  // open: nQ
  Button ESCREVER (.out(ESCREVER_out));
  and and_2 (and_2_out, Cp, and_1_out, jk_ff_as_1_q[1]);
  JK_FF_AS jk_ff_as_2 (
    .Set(1'b0), .J(and_1_out), .C(in_10), .K(and_1_out), .Clr(CLR), .Q(jk_ff_as_1_q[1]));  // open: nQ
  D_FF_AS d_ff_as_2 (.Set(1'b0), .D(driver_2_out[2]), .C(in_10), .Clr(CLR_2), .Q(d_ff_as_1_q[2]));  // open: nQ
  Multiplexer #(.Bits(4)) multiplexer_1 (.sel(RUN), .in_0(ENDE), .in_1(d_ff_as_1_q), .out(multiplexer_1_out));
  and and_3 (and_3_out, Cp, and_2_out, jk_ff_as_1_q[2]);
  JK_FF_AS jk_ff_as_3 (
    .Set(1'b0), .J(and_2_out), .C(in_10), .K(and_2_out), .Clr(CLR), .Q(jk_ff_as_1_q[2]));  // open: nQ
  D_FF_AS d_ff_as_3 (.Set(1'b0), .D(driver_2_out[1]), .C(in_10), .Clr(CLR_2), .Q(d_ff_as_1_q[1]));  // open: nQ
  not not_1 (not_1_out, RUN);
  and and_4 (and_4_out, ~RUN, ESCREVER_out);  // And
  JK_FF_AS jk_ff_as_4 (
    .Set(1'b0), .J(and_3_out), .C(in_10), .K(and_3_out), .Clr(CLR), .Q(jk_ff_as_1_q[3]));  // open: nQ
  D_FF_AS d_ff_as_4 (.Set(1'b0), .D(driver_2_out[0]), .C(in_10), .Clr(CLR_2), .Q(d_ff_as_1_q[0]));  // open: nQ
  RAMDualPort #(.AddrBits(4), .Bits(8)) ramdualport_1 (
    .A(multiplexer_1_out), .Din(DADO), .str(not_1_out), .C(and_4_out), .ld(CE), .D(ramdualport_1_d));
  assign ramdualport_1_d[3:0] = Ep ? jk_ff_as_1_q : 4'bz;  // Driver driver_1
  assign driver_2_out = not_2_out ? ramdualport_1_d[3:0] : 4'bz;  // Driver driver_2
  not not_2 (not_2_out, LM);
  // Probe on ramdualport_1_d[4]
  // Probe on ramdualport_1_d[7]
  // Probe on ramdualport_1_d[6]
  // Probe on ramdualport_1_d[5]
  // Probe on ramdualport_1_d[3]
  // Probe on ramdualport_1_d[2]
  // Probe on ramdualport_1_d[1]
  // Probe on ramdualport_1_d[0]

  // Notes on the sheet:
  //   CONTADOR
  //   REM
  //   RAM
endmodule
