// Digital circuit SAP1.dig as structural Verilog
module SAP1 (
  input  in_1,
  input  clk,
  input  in_3,
  input  in_4,
  input  in_5,
  input  clk_2,
  input  in_7
);

  wire and_1_out, button_1_out, button_2_out, CLR_out, jk_ff_1_q, jk_ff_2_q, jk_ff_3_q, jk_ff_4_q,
       jk_ff_as_1_q, nand_1_out, nand_2_out, nand_3_out, nand_4_out, nand_5_out, nand_6_out, nand_7_out,
       nand_8_out, nand_9_out, nand_10_out, nand_11_out, nand_12_out, nand_13_out, nand_14_out, nand_15_out,
       nand_16_out, nand_17_out, nand_18_out, nand_19_out, nand_20_out, nand_21_out, nand_22_out,
       nand_23_out, nand_24_out, nand_25_out, nand_26_out, nand_27_out, nand_28_out, nand_29_out,
       nand_30_out, nand_31_out, nand_32_out, not_1_out, not_2_out, not_3_out, not_4_out, not_5_out,
       not_6_out, SET_out;

  // Probe on nand_31_out
  // Probe on nand_23_out
  // Probe on nand_15_out
  and and_1 (and_1_out, in_7, clk_2);
  // Probe on nand_7_out
  not not_1 (not_1_out, SET_out);
  Button SET (.out(SET_out));
  nand nand_1 (nand_1_out, nand_8_out, in_5, and_1_out);
  nand nand_2 (nand_2_out, and_1_out, in_5, nand_7_out);
  Button CLR (.out(CLR_out));
  not not_2 (not_2_out, CLR_out);
  nand nand_3 (nand_3_out, not_1_out, nand_1_out, nand_4_out);
  nand nand_4 (nand_4_out, nand_3_out, nand_2_out, not_2_out);
  not not_3 (not_3_out, and_1_out);
  nand nand_5 (nand_5_out, not_2_out, nand_3_out, not_3_out);
  nand nand_6 (nand_6_out, not_3_out, nand_4_out, not_1_out);
  nand nand_7 (nand_7_out, not_1_out, nand_5_out, nand_8_out);
  nand nand_8 (nand_8_out, nand_7_out, nand_6_out, not_2_out);
  JK_FF jk_ff_1 (.J(in_1), .C(~clk), .K(in_1), .Q(jk_ff_1_q));  // open: nQ
  LED led_1 (.in(jk_ff_1_q));
  JK_FF jk_ff_2 (.J(in_1), .C(~jk_ff_1_q), .K(in_1), .Q(jk_ff_2_q));  // open: nQ
  LED led_2 (.in(jk_ff_2_q));
  nand nand_9 (nand_9_out, nand_16_out, in_5, nand_7_out);
  nand nand_10 (nand_10_out, nand_7_out, in_5, nand_15_out);
  JK_FF jk_ff_3 (.J(in_1), .C(~jk_ff_2_q), .K(in_1), .Q(jk_ff_3_q));  // open: nQ
  nand nand_11 (nand_11_out, not_1_out, nand_9_out, nand_12_out);
  nand nand_12 (nand_12_out, nand_11_out, nand_10_out, not_2_out);
  LED led_3 (.in(jk_ff_3_q));
  not not_4 (not_4_out, nand_7_out);
  JK_FF jk_ff_4 (.J(in_1), .C(~jk_ff_3_q), .K(in_1), .Q(jk_ff_4_q));  // open: nQ
  nand nand_13 (nand_13_out, not_2_out, nand_11_out, not_4_out);
  nand nand_14 (nand_14_out, not_4_out, nand_12_out, not_1_out);
  LED led_4 (.in(jk_ff_4_q));
  nand nand_15 (nand_15_out, not_1_out, nand_13_out, nand_16_out);
  nand nand_16 (nand_16_out, nand_15_out, nand_14_out, not_2_out);
  Button button_1 (.out(button_1_out));
  Button button_2 (.out(button_2_out));
  JK_FF_AS jk_ff_as_1 (
    .Set(button_2_out), .J(in_4), .C(~in_3), .K(in_4), .Clr(button_1_out), .Q(jk_ff_as_1_q));  // open: nQ
  nand nand_17 (nand_17_out, nand_24_out, in_5, nand_15_out);
  nand nand_18 (nand_18_out, nand_15_out, in_5, nand_23_out);
  LED led_5 (.in(jk_ff_as_1_q));
  nand nand_19 (nand_19_out, not_1_out, nand_17_out, nand_20_out);
  nand nand_20 (nand_20_out, nand_19_out, nand_18_out, not_2_out);
  not not_5 (not_5_out, nand_15_out);
  nand nand_21 (nand_21_out, not_2_out, nand_19_out, not_5_out);
  nand nand_22 (nand_22_out, not_5_out, nand_20_out, not_1_out);
  nand nand_23 (nand_23_out, not_1_out, nand_21_out, nand_24_out);
  nand nand_24 (nand_24_out, nand_23_out, nand_22_out, not_2_out);
  nand nand_25 (nand_25_out, nand_32_out, in_5, nand_23_out);
  nand nand_26 (nand_26_out, nand_23_out, in_5, nand_31_out);
  nand nand_27 (nand_27_out, not_1_out, nand_25_out, nand_28_out);
  nand nand_28 (nand_28_out, nand_27_out, nand_26_out, not_2_out);
  not not_6 (not_6_out, nand_23_out);
  nand nand_29 (nand_29_out, not_2_out, nand_27_out, not_6_out);
  nand nand_30 (nand_30_out, not_6_out, nand_28_out, not_1_out);
  nand nand_31 (nand_31_out, not_1_out, nand_29_out, nand_32_out);
  nand nand_32 (nand_32_out, nand_31_out, nand_30_out, not_2_out);
endmodule
